# Fritzing sketch sensor_w_nrf24l01_prototype (saved by Fritzing 0.9.0b)
circuit board: 4.289cm x 2.03417cm
breadboards: 1

parts:
  U1 = atmega328 [package=dip]
  R1 = Photocell (LDR) [package=THT]
  R2 = Resistor [tolerance=±5% resistance=220 package=THT]
  V1 = DC Power [voltage=3.3V]
  J1 = Screw terminal - 2 pins [package=THT]
  NRF24L1 = NRF24L01

nets (from the schematic view):
  VCC: U1.VCC, U1.AVCC, R1.pin_0, V1.V+, J1.pin2, NRF24L1.VCC
  N1: U1.GND#7, R2.Pin_1, V1.V-, J1.pin1, NRF24L1.GND
  N2: U1.D9_(PWM), NRF24L1.CE
  N3: U1.D10_(PWM), NRF24L1.CSN
  N4: U1.D11_(PWM), NRF24L1.MOSI
  N5: U1.D12, NRF24L1.MISO
  N6: U1.D13, NRF24L1.SCK
  N7: U1.A0, R1.pin_1, R2.Pin_0

custom parts:
  NRF24L01: NRF24L01 module
